# Fritzing sketch DemoSetUp (saved by Fritzing 0.9.4)
breadboards: 2

parts:
  WeMos_D1_Mini1 = WeMos D1 Mini
  OLED_I2C1 = OLED 128x64 I2C Monochrome Display
  WeMos_D1_Mini2 = WeMos D1 Mini
  WeMos_D1_Mini3 = WeMos D1 Mini
  WeMos_D1_Mini4 = WeMos D1 Mini
  OLED_I2C2 = OLED 128x64 I2C Monochrome Display
  OLED_I2C3 = OLED 128x64 I2C Monochrome Display
  LED1 = smd LED [color="White (4500K)" package="0603 [SMD]"]
  LED2 = smd LED [color="Blue (525nm)" package="0805 [SMD]"]
  R1 = Resistor [tolerance=±5% resistance=681 package=THT]
  R2 = Resistor [tolerance=±5% resistance=681 package=THT]
  LED3 = smd LED [color="Green (565nm)" package="0805 [SMD]"]
  LED4 = smd LED [color="Red (635nm)" package="0805 [SMD]"]
  R3 = Resistor [tolerance=±5% resistance=681 package=THT]
  R4 = Resistor [tolerance=±5% resistance=681 package=THT]

nets:
  3V3: WeMos_D1_Mini1.3V3, OLED_I2C3.VDD
  N1: WeMos_D1_Mini1.D0, R4.Pin_0
  N2: WeMos_D1_Mini1.D5, R3.Pin_0
  N3: WeMos_D1_Mini1.D6, R1.Pin_0
  N4: WeMos_D1_Mini1.G, LED2.cathode, LED3.cathode, LED4.cathode
  N5: WeMos_D1_Mini1.RX, WeMos_D1_Mini2.TX
  N6: WeMos_D1_Mini1.TX, WeMos_D1_Mini2.RX
  N7: OLED_I2C1.SDA, WeMos_D1_Mini2.D1
  N8: OLED_I2C1.SCK, WeMos_D1_Mini2.D2
  VDD: OLED_I2C1.VDD, OLED_I2C2.VDD
  GND: OLED_I2C1.GND, WeMos_D1_Mini2.G, WeMos_D1_Mini4.G, OLED_I2C2.GND, LED1.cathode
  3V3_2: WeMos_D1_Mini2.3V3, WeMos_D1_Mini4.3V3
  N9: WeMos_D1_Mini2.D0, R2.Pin_1
  N10: WeMos_D1_Mini3.D1, OLED_I2C3.SDA
  N11: WeMos_D1_Mini3.D2, OLED_I2C3.SCK
  N12: WeMos_D1_Mini3.G, OLED_I2C3.GND
  N13: WeMos_D1_Mini4.D1, OLED_I2C2.SDA
  N14: WeMos_D1_Mini4.D2, OLED_I2C2.SCK
  N15: LED1.anode, R2.Pin_0
  N16: LED2.anode, R1.Pin_1
  N17: LED3.anode, R3.Pin_1
  N18: LED4.anode, R4.Pin_1
